# Fritzing sketch TCS-750-i2c-ard (saved by Fritzing 0.9.9b)
circuit board: 8.46667cm x 5.64444cm

parts:
  J1_A = female pin header, 11 pins [form="♀ (female)"]
  J2_A = female pin header, 11 pins [form="♀ (female)"]
  J1_B = female pin header, 11 pins [form="♀ (female)"]
  A1 = Arduino proto shield
  J2_B = female pin header, 11 pins [form="♀ (female)"]
  R1 = Resistor [tolerance=±10% power=0.25 resistance=4.7k part_number=(opt) package=THT]
  R2 = Resistor [tolerance=±10% power=0.25 resistance=4.7k part_number=(opt) package=THT]
  S1 = Toggle Switch [package=THT]

nets:
  N1: J1_A.pin1, J1_A.pin11, J1_B.pin1, J1_B.pin11, A1.Pin_212, A1.Pin_275, A1.Pin_276, A1.Pin_416, A1.Pin_417, A1.Pin_440, A1.Pin_454, R1.Pin_1, R2.Pin_1, S1.COM
  N2: J1_A.pin2, J1_B.pin2, A1.Pin_289, A1.Pin_290
  N3: J1_A.pin3, J1_B.pin3, A1.Pin_303, A1.Pin_304
  N4: J1_A.pin4, J1_B.pin4, A1.Pin_317, A1.Pin_318
  N5: J1_A.pin5, J1_B.pin5, A1.Pin_28, A1.Pin_63, A1.Pin_331, A1.Pin_332, A1.Pin_458, R1.Pin_0
  N6: J1_A.pin6, J1_B.pin6, A1.Pin_26, A1.Pin_61, A1.Pin_345, A1.Pin_346, A1.Pin_444, R2.Pin_0
  N7: J1_A.pin7, J1_B.pin7, A1.Pin_47, A1.Pin_359, A1.Pin_360
  N8: J1_A.pin8, J1_B.pin8, A1.Pin_373, A1.Pin_374
  N9: J1_A.pin9, J1_B.pin9, A1.Pin_388, A1.Pin_389
  N10: J1_A.pin10, J1_B.pin10, A1.Pin_402, A1.Pin_403
  N11: J2_A.pin1, A1.Pin_407, A1.Pin_408, J2_B.pin1
  N12: J2_A.pin2, A1.Pin_393, A1.Pin_394, J2_B.pin2
  N13: J2_A.pin3, A1.Pin_379, A1.Pin_380, J2_B.pin3
  N14: J2_A.pin4, A1.Pin_364, A1.Pin_365, J2_B.pin4
  N15: J2_A.pin5, A1.Pin_350, A1.Pin_351, J2_B.pin5
  N16: J2_A.pin6, A1.Pin_336, A1.Pin_337, J2_B.pin6
  N17: J2_A.pin7, A1.Pin_322, A1.Pin_323, J2_B.pin7
  N18: J2_A.pin8, A1.Pin_309, J2_B.pin8
  N19: J2_A.pin9, A1.Pin_294, A1.Pin_295, J2_B.pin9
  N20: J2_A.pin10, A1.Pin_45, A1.Pin_46, A1.Pin_280, A1.Pin_281, J2_B.pin10
  N21: J2_A.pin11, A1.Pin_11, A1.Pin_12, A1.Pin_13, A1.Pin_57, A1.Pin_58, A1.Pin_266, A1.Pin_267, J2_B.pin11
  N22: A1.Pin_8, A1.Pin_213, S1.L1
  N23: A1.Pin_9, A1.Pin_10, A1.Pin_211, S1.L2

notes:
  nRST
  GND
  I2C/nSPI
  SCL/SCK
  SDA/Vss
  nIRQ
  Vin
  A4/SCL
  A5/SDA
  D8
  D9
  3V3
  5V0
  A0/nCS
  A1/SDI
  nc/SDO
  IO0
  IO1
  IO2
  IO3
  IO4
  IO5
  IO6
  IO7
  RTS
  CTS
  TxD
  RxD
  RESET
  Vss/GND
  TCS-75x, TCS-750-i2c-ard – CJMCU-750 over I2C on Arduino UNO R3, 0.1
  D10/SS
  D11/COPI
  D12/CIPO
  D13/SCK
  TCS-750-i2c-ard R0.1

custom parts:
  Arduino proto shield: Arduino proto shield.
