# Fritzing sketch x_grove_testbed (saved by Fritzing 0.9.9b)

parts:
  M1 = Grove Base Shield - V2
  Grove_LED1 = Grove LED Socket Kit [part_number=SKU-104030005]
  Grove_BTN1 = Grove Button [part_number=SKU-101020003]

nets:
  N1: M1.pin_104, M1.pin_108, M1.pin_112, Grove_LED1.Pin_4, Grove_BTN1.Pin_4
  N2: M1.pin_105, M1.pin_113, M1.pin_125, Grove_LED1.Pin_3, Grove_BTN1.Pin_3
  N3: M1.pin_106, M1.pin_111, Grove_BTN1.Pin_2
  N4: M1.pin_107, Grove_BTN1.Pin_1
  N5: M1.pin_110, M1.pin_115, Grove_LED1.Pin_1
  N6: M1.pin_114, Grove_LED1.Pin_2

custom parts:
  Grove Base Shield - V2: Base Shield V2 vanepp jan 2018: fix up schematic for someone in the forums.
  Grove LED Socket Kit: A general-purpose LED module in Grove form factor, available in different colors. Support adjustable LED orientation and adjustable LED brightness.
  Grove Button: Grove - Button is a momentary push button. It contains one independent "momentary on/off" button. "Momentary" means that the button rebounds on its own after it is released.
